# Fritzing sketch Button PCB (saved by Fritzing 0.9.0b)
circuit board: 5.9737cm x 2.74101cm
breadboards: 1

parts:
  S1 = SWITCH-MOMENTARY-2 [package=tactile-pth]
  S2 = SWITCH-MOMENTARY-2 [package=tactile-pth]
  S3 = SWITCH-MOMENTARY-2 [package=tactile-pth]
  S4 = SWITCH-MOMENTARY-2 [package=tactile-pth]
  J1 = female pin header, 5 pins [form="♀ (female)"]

nets:
  N1: S1.1, S2.1, S3.1, S4.1, J1.pin1
  N2: S1.2, J1.pin2
  N3: S2.2, J1.pin3
  N4: S3.2, J1.pin4
  N5: S4.2, J1.pin5

notes:
  ACFC  Button-PCB
  SW4
  SW3
  SW2
  SW1
  SW5V
