# Fritzing sketch Main PCB (saved by Fritzing 0.9.0b)
circuit board: 6.98808cm x 6.56726cm
breadboards: 1

parts:
  J1 = female pin header, 8 pins [form="♀ (female)"]
  J2 = female pin header, 8 pins [form="♀ (female)"]
  J4 = female pin header, 6 pins [form="♀ (female)"]
  R1 = Resistor [tolerance=±5% resistance=10k package=THT]
  R2 = Resistor [tolerance=±5% resistance=10k package=THT]
  R3 = Resistor [tolerance=±5% resistance=10k package=THT]
  R4 = Resistor [tolerance=±5% resistance=10k package=THT]
  R5 = Resistor [tolerance=±5% resistance=10k package=THT]
  J5 = female pin header, 8 pins [form="♀ (female)"]
  J6 = female pin header, 8 pins [form="♀ (female)"]
  R6 = Resistor [tolerance=±5% resistance=3k package=THT]
  C1 = Electrolytic Capacitor [capacitance=100µF package="200 mil [THT, electrolytic]"]
  J7 = female pin header, 5 pins [form="♀ (female)"]
  J3 = female pin header, 6 pins [form="♀ (female)"]  # not connected
  VIN = Battery

nets:
  N1: J1.pin1, J5.pin1
  N2: J1.pin2, J5.pin2
  N3: J1.pin3, J5.pin3
  N4: J1.pin4, J5.pin4
  N5: J1.pin5, J5.pin5
  N6: J1.pin6, J5.pin6
  N7: J1.pin7, J5.pin7
  N8: J1.pin8, J5.pin8
  N9: J2.pin2, J6.pin2, R6.Pin_0, J7.pin3, J7.pin5
  N10: J2.pin3, J6.pin3
  N11: J2.pin4, R5.Pin_1, J6.pin4
  N12: J2.pin5, R4.Pin_1, J6.pin5
  N13: J2.pin6, R3.Pin_1, J6.pin6
  N14: J2.pin7, R2.Pin_1, J6.pin7
  N15: J2.pin8, R1.Pin_1, J6.pin8
  N16: J4.pin3, J6.pin1, C1.+, J7.pin1, J7.pin2
  N17: J4.pin4, R1.Pin_0, R2.Pin_0, R3.Pin_0, R4.Pin_0, R5.Pin_0, C1.-
  N18: J4.pin5, VIN.-
  N19: J4.pin6, VIN.+
  N20: R6.Pin_1, J7.pin4

notes:
  RX-0
  TX-1
  D02
  D03
  D04
  D05
  D07
  D06
  D08
  D09
  D10
  D11
  D12
  D13
  GND
  AREF
  A5
  A4
  A3
  A2
  A1
  A0
  VIN
  5V
  3V
  RESET
  9V
  10k
  3k
  10uF
  +
  RL12
  RL04
  SW1
  SW2
  SW3
  SW4
  LD15
  LD16
  LD02
  LD01
  LD03
  LD05
  LD14
  LD13
  LD12
  LD11
  LD06
  LD04
  -
  SW5V
  Main-PCB
  ACFC
