# Fritzing sketch Schematic Diagram (saved by Fritzing 0.9.1b)
breadboards: 1

parts:
  Part1 = Arduino Uno (Rev3)
  U1 = LCD-16X2 [package=lcd-16x2_noholes]
  C1 = Electrolytic Capacitor [capacitance=10µF package="100 mil [THT, electrolytic]"]
  R6 = Resistor [tolerance=±5% resistance=3k package="0805 [SMD]"]
  R1 = Resistor [tolerance=±5% resistance=10k package="0805 [SMD]"]
  R2 = Resistor [tolerance=±5% resistance=10k package="0805 [SMD]"]
  R3 = Resistor [tolerance=±5% resistance=10k package="0805 [SMD]"]
  R4 = Resistor [tolerance=±5% resistance=10k package="0805 [SMD]"]
  R5 = Resistor [tolerance=±5% resistance=10k package="0805 [SMD]"]
  RELAY_220VAC = RELAY-2 [package=relay-g5v]
  AC_Mains = AC Power [voltage=220 frequency=60]
  F1_10A = FUSE [package=fuse_5mm]
  D12/MISO = female pin header, 1 pin [form="♀ (female)"]
  SW1 = SWITCH-MOMENTARY-2 [package=tactile_switch_tall]
  SW2 = SWITCH-MOMENTARY-2 [package=tactile_switch_tall]
  SW4 = SWITCH-MOMENTARY-2 [package=tactile_switch_tall]
  SW3 = SWITCH-MOMENTARY-2 [package=tactile_switch_tall]
  D8 = female pin header, 1 pin [form="♀ (female)"]
  D9_PWM = female pin header, 1 pin [form="♀ (female)"]
  D10_PWM/SS = female pin header, 1 pin [form="♀ (female)"]
  D11_PWM/MOSI = female pin header, 1 pin [form="♀ (female)"]
  VIN = DC Power [voltage=9]

nets:
  N1: Part1.D8, R1.Pin_0
  N2: Part1.D9_PWM, R2.Pin_0
  N3: Part1.D10_PWM/SS, R3.Pin_0
  N4: Part1.D11_PWM/MOSI, R4.Pin_0
  N5: Part1.D12/MISO, R5.Pin_0
  N6: Part1.D13/SCK, U1.A
  GND: Part1.GND, U1.VSS, U1.R_W, U1.K, C1.-, R6.Pin_0, R1.Pin_1, R2.Pin_1, R3.Pin_1, R4.Pin_1, R5.Pin_1, VIN.V-
  N7: Part1.D2, U1.DB7
  N8: Part1.D3_PWM, U1.DB6
  N9: Part1.D4, U1.DB5
  N10: Part1.D5_PWM, U1.DB4
  N11: Part1.D6_PWM, U1.E
  N12: Part1.D7, U1.RS
  5V: Part1.5V, U1.VDD, C1.+
  N13: Part1.VIN, VIN.V+
  N14: U1.VO, R6.Pin_1
  N15: RELAY_220VAC.2, AC_Mains.V-
  5V_2: RELAY_220VAC.5, SW1.1, SW2.1, SW4.1, SW3.1
  N16: RELAY_220VAC.9, F1_10A.1
  N17: RELAY_220VAC.10, D12/MISO.pin1
  N18: AC_Mains.V+, F1_10A.2
  N19: SW1.2, D8.pin1
  N20: SW2.2, D9_PWM.pin1
  N21: SW4.2, D11_PWM/MOSI.pin1
  N22: SW3.2, D10_PWM/SS.pin1

notes:
  4
  12
  NC
  NO
